# Fritzing sketch FreezerTempMonitor (saved by Fritzing 0.9.3b)
circuit board: 4.15296cm x 3.74356cm

parts:
  R2 = Resistor [tolerance=±5% resistance=220 package=THT]
  R3 = Resistor [tolerance=±5% resistance=4.7k package=THT]
  DS2 = DS18B20 1-Wire Temperature Sensor [part_number=DS18B20]
  LED1 = LED - 3mm [color="Red (633nm)" package="3 mm [THT]"]
  LED2 = LED - 3mm [color="Green (555nm)" package="3 mm [THT]"]
  R1 = Resistor [tolerance=±5% resistance=100 package=THT]
  WeMos_D1_Mini2 = WeMos D1 Mini

nets:
  N1: R2.Pin_0, WeMos_D1_Mini2.D0
  N2: R2.Pin_1, LED1.anode
  N3: R3.Pin_0, DS2.DQ, WeMos_D1_Mini2.D1
  VDD: R3.Pin_1, DS2.VDD, WeMos_D1_Mini2.5V
  N4: DS2.GND, LED1.cathode, LED2.cathode, WeMos_D1_Mini2.G
  N5: LED2.anode, R1.Pin_1
  N6: R1.Pin_0, WeMos_D1_Mini2.D2

notes:
  FreezerTempMonitor
  v1.0
